# Fritzing sketch Connection (saved by Fritzing 0.9.3b)
breadboards: 2

parts:
  WeMos_D1_Mini1 = WeMos D1 Mini
  Composant1 = ws2812b [package="smd 2812b"]
  Composant2 = ws2812b [package="smd 2812b"]
  Composant3 = ws2812b [package="smd 2812b"]
  Composant4 = ws2812b [package="smd 2812b"]
  Composant5 = ws2812b [package="smd 2812b"]
  Composant6 = ws2812b [package="smd 2812b"]
  Composant7 = ws2812b [package="smd 2812b"]
  Composant8 = ws2812b [package="smd 2812b"]
  Composant9 = ws2812b [package="smd 2812b"]
  Composant10 = ws2812b [package="smd 2812b"]
  Composant11 = ws2812b [package="smd 2812b"]
  Composant12 = ws2812b [package="smd 2812b"]
  Composant13 = ws2812b [package="smd 2812b"]
  Composant14 = ws2812b [package="smd 2812b"]

nets:
  VDD: WeMos_D1_Mini1.5V, Composant1.VDD, Composant2.VDD, Composant10.VDD, Composant11.VDD, Composant12.VDD, Composant13.VDD, Composant14.VDD
  VSS: WeMos_D1_Mini1.G, Composant1.VSS, Composant2.VSS, Composant3.VSS, Composant4.VSS, Composant5.VSS, Composant6.VSS, Composant7.VSS, Composant8.VSS, Composant9.VSS, Composant10.VSS, Composant11.VSS, Composant12.VSS, Composant13.VSS, Composant14.VSS
